# Fritzing sketch CanisHerz (saved by Fritzing 0.9.3b)

parts:
  TP1 = TP4056 [chip_label=TP4056 package="DIP (Dual Inline) [THT]"]
  M2 = DOIT Esp32 DevKit v1 (30 pins long, 11 pins width) [part_number=ESP32S-PIN30]
  BAT1 = 18650 battery holder [package=battery-18650-kit]
  M3 = GY-MAX30102
  R1 = Resistor [tolerance=±5% resistance=100 package=THT]
  R2 = Resistor [tolerance=±5% resistance=100 package=THT]

nets:
  N1: TP1.pin3, M2.VIN, R1.Pin_0
  N2: TP1.pin4, BAT1.-
  N3: TP1.pin5, BAT1.+
  GND: TP1.pin6, M2.GND, M3.GND, R2.Pin_1
  3V3: M2.3V3, M3.VIN
  N4: M2.D21, M3.SDA
  N5: M2.D22, M3.SCL
  N6: M2.D33, R1.Pin_1, R2.Pin_0

custom parts:
  TP4056: A DIP stand-in part for whatever IC you want. With 6 pins on a 300mil dual inline package (DIP) footprint.
  DOIT Esp32 DevKit v1 (30 pins long, 11 pins width): The DOIT Esp32 DevKit v1 is one of the development board created by DOIT to evaluate the ESP-WROOM-32 module. It is based on the ESP32 microcontroller that boasts Wifi, Bluetooth, Ethernet and Low Power support all in a single chip. (vanepp) made breadboard work, adjusted pin numbering and labels and reduced size of schematic and cleaned up pcb. This chip is 30pins long (2 x15) and 11 pins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
  18650 battery holder: 18650 Battery
  GY-MAX30102: Oximeter module using the MAX30102 chip. You may wish to read (and check your module) this post on power problems with these modules: https://reedpaper.wordpress.com/2018/08/22/pulse-oximeter-max30100-max30102-how-to-fix-wrong-board/ (may not apply as this is a different module!). As usual, if you want the mounting holes in pcb, you need to drag a hole over the pad in silkscreen to actually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
